// Logisim project DSFFinal2.circ as structural Verilog: 1 circuit, main circuit main
module main (
  input  MOVE_FROM_B,
  input  MOVE_FROM_B_2,
  input  MOVE_TO_B,
  input  MOVE_TO_B_2
);

  wire and_1_out, and_2_out, and_3_out, and_4_out, and_5_out, and_6_out, and_7_out, and_8_out, and_9_out,
       and_10_out, and_11_out, and_12_out, and_13_out, and_14_out, and_15_out, and_16_out, and_17_out,
       and_18_out, and_19_out, and_20_out, and_21_out, and_22_out, and_23_out, and_24_out, and_25_out,
       and_26_out, and_27_out, and_28_out, and_29_out, and_30_out, and_31_out, and_32_out, and_33_out,
       and_34_out, and_35_out, and_36_out, button_1_out, button_2_out, clock_1_out, controlled_buffer_1_out,
       counter_1_carry, counter_2_carry, d_ff_1_q, d_ff_2_q, d_ff_3_q, d_ff_4_q, d_ff_5_q, d_ff_6_q,
       d_ff_7_q, d_ff_8_q, multiplexer_1_out, multiplexer_2_out, multiplexer_3_out, multiplexer_4_out,
       multiplexer_5_out, multiplexer_6_out, multiplexer_7_out, multiplexer_8_out, or_1_out, or_2_out,
       or_3_out, or_4_out, shift_register_1_out, shift_register_1_q0, shift_register_1_q1,
       shift_register_1_q2, shift_register_1_q3, shift_register_2_out, shift_register_2_q0,
       shift_register_2_q1, shift_register_2_q2, shift_register_2_q3, shift_register_3_out,
       shift_register_3_q0, shift_register_3_q1, shift_register_3_q2, shift_register_3_q3,
       shift_register_4_out, shift_register_4_q0, shift_register_4_q1, shift_register_4_q2,
       shift_register_4_q3, shift_register_5_out, shift_register_5_q0, shift_register_5_q1,
       shift_register_5_q2, shift_register_5_q3, shift_register_6_out, shift_register_6_q0,
       shift_register_6_q1, shift_register_6_q2, shift_register_6_q3, shift_register_7_out,
       shift_register_7_q0, shift_register_7_q1, shift_register_7_q2, shift_register_7_q3,
       shift_register_8_out, shift_register_8_q0, shift_register_8_q1, shift_register_8_q2,
       shift_register_8_q3, xnor_1_out, xor_1_out, xor_2_out, xor_3_out, xor_4_out, xor_5_out, xor_6_out,
       xor_7_out, xor_8_out;
  wire [1:0] counter_2_q;

  or or_1 (or_1_out, button_1_out, ~counter_1_carry);  // OR_Gate
  and and_1 (and_1_out, or_1_out, clock_1_out);
  Button button_1 (.out(button_1_out));
  Counter #(.width(2), .max('h3)) counter_1 (.carry(counter_1_carry), .clk(and_1_out));  // open: load, D, count, Q, clr
  Clock clock_1 (.out(clock_1_out));
  or or_2 (or_2_out, button_2_out, ~counter_2_carry);  // OR_Gate
  and and_2 (and_2_out, or_2_out, clock_1_out);
  Button button_2 (.out(button_2_out));
  Counter #(.width(2), .max('h3)) counter_2 (
    .Q(counter_2_q), .carry(counter_2_carry), .clk(and_2_out));  // open: load, D, count, clr
  and and_3 (and_3_out, counter_2_q[0], counter_2_q[1], button_2_out);
  xnor xnor_1 (xnor_1_out, counter_2_q[0], counter_2_q[1]);
  or or_3 (or_3_out, counter_2_q[0], ~counter_2_q[1]);  // OR_Gate
  or or_4 (or_4_out, and_1_out, and_2_out);
  and and_4 (and_4_out, xnor_1_out, button_2_out);
  and and_5 (and_5_out, button_2_out, or_3_out);
  and and_6 (and_6_out, button_2_out, 1'b1);
  Multiplexer #(.enable("false")) multiplexer_1 (
    .in0(and_3_out), .in1(controlled_buffer_1_out), .out(multiplexer_1_out), .sel(MOVE_TO_B));
  Multiplexer #(.enable("false")) multiplexer_2 (
    .in0(and_4_out), .in1(controlled_buffer_1_out), .out(multiplexer_2_out), .sel(and_11_out));
  Multiplexer #(.enable("false")) multiplexer_3 (
    .in0(and_5_out), .in1(controlled_buffer_1_out), .out(multiplexer_3_out), .sel(MOVE_TO_B));
  Multiplexer #(.enable("false")) multiplexer_4 (
    .in0(and_6_out), .in1(controlled_buffer_1_out), .out(multiplexer_4_out), .sel(MOVE_TO_B));
  and and_7 (and_7_out, MOVE_TO_B, ~and_8_out, ~and_9_out, ~and_11_out, ~shift_register_1_q3);  // AND_Gate
  and and_8 (and_8_out, MOVE_TO_B, ~and_11_out, ~and_9_out, ~shift_register_2_q3);  // AND_Gate
  and and_9 (and_9_out, MOVE_TO_B, ~and_11_out, ~shift_register_3_q3);  // AND_Gate
  and and_10 (and_10_out, d_ff_4_q, MOVE_FROM_B);
  and and_11 (and_11_out, MOVE_TO_B, ~shift_register_4_q3);  // AND_Gate
  and and_12 (and_12_out, d_ff_1_q, MOVE_FROM_B);
  and and_13 (and_13_out, d_ff_2_q, MOVE_FROM_B);
  and and_14 (and_14_out, d_ff_3_q, MOVE_FROM_B);
  ExactlyOne xor_1 (.out(xor_1_out), .in0(and_10_out), .in1(or_2_out), .in2(and_11_out));
  Shift_Register #(.length(4)) shift_register_1 (
    .in(multiplexer_1_out), .clk(and_15_out), .out(shift_register_1_out), .q0(shift_register_1_q0),
    .q1(shift_register_1_q1), .q2(shift_register_1_q2), .q3(shift_register_1_q3));  // open: shift, load, clr, d0, d1, d2, d3
  ExactlyOne xor_2 (.out(xor_2_out), .in0(and_12_out), .in1(or_2_out), .in2(and_7_out));
  and and_15 (and_15_out, xor_2_out, or_4_out);
  Shift_Register #(.length(4)) shift_register_2 (
    .in(multiplexer_2_out), .clk(and_16_out), .out(shift_register_2_out), .q0(shift_register_2_q0),
    .q1(shift_register_2_q1), .q2(shift_register_2_q2), .q3(shift_register_2_q3));  // open: shift, load, clr, d0, d1, d2, d3
  ExactlyOne xor_3 (.out(xor_3_out), .in0(and_13_out), .in1(or_2_out), .in2(and_8_out));
  and and_16 (and_16_out, xor_3_out, or_4_out);
  Shift_Register #(.length(4)) shift_register_3 (
    .in(multiplexer_3_out), .clk(and_17_out), .out(shift_register_3_out), .q0(shift_register_3_q0),
    .q1(shift_register_3_q1), .q2(shift_register_3_q2), .q3(shift_register_3_q3));  // open: shift, load, clr, d0, d1, d2, d3
  ExactlyOne xor_4 (.out(xor_4_out), .in0(and_14_out), .in1(or_2_out), .in2(and_9_out));
  and and_17 (and_17_out, xor_4_out, or_4_out);
  Shift_Register #(.length(4)) shift_register_4 (
    .in(multiplexer_4_out), .clk(and_18_out), .out(shift_register_4_out), .q0(shift_register_4_q0),
    .q1(shift_register_4_q1), .q2(shift_register_4_q2), .q3(shift_register_4_q3));  // open: shift, load, clr, d0, d1, d2, d3
  and and_18 (and_18_out, xor_1_out, or_4_out);
  DotMatrix #(.matrixcols(7), .matrixrows(1)) dotmatrix_1 (
    .col0(shift_register_1_q0), .col1(shift_register_1_q1), .col2(shift_register_1_q2),
    .col3(shift_register_1_q3), .col4(shift_register_1_q2), .col5(shift_register_1_q1),
    .col6(shift_register_1_q0));
  DotMatrix #(.matrixcols(7), .matrixrows(1)) dotmatrix_2 (
    .col0(shift_register_2_q0), .col1(shift_register_2_q1), .col2(shift_register_2_q2),
    .col3(shift_register_2_q3), .col4(shift_register_2_q2), .col5(shift_register_2_q1),
    .col6(shift_register_2_q0));
  DotMatrix #(.matrixcols(7), .matrixrows(1)) dotmatrix_3 (
    .col0(shift_register_3_q0), .col1(shift_register_3_q1), .col2(shift_register_3_q2),
    .col3(shift_register_3_q3), .col4(shift_register_3_q2), .col5(shift_register_3_q1),
    .col6(shift_register_3_q0));
  DotMatrix #(.matrixcols(7), .matrixrows(1)) dotmatrix_4 (
    .col0(shift_register_4_q0), .col1(shift_register_4_q1), .col2(shift_register_4_q2),
    .col3(shift_register_4_q3), .col4(shift_register_4_q2), .col5(shift_register_4_q1),
    .col6(shift_register_4_q0));
  and and_19 (and_19_out, shift_register_2_q3, ~shift_register_1_q3);  // AND_Gate
  and and_20 (and_20_out, shift_register_3_q3, ~shift_register_2_q3, ~shift_register_1_q3);  // AND_Gate
  and and_21 (and_21_out, shift_register_4_q3, ~shift_register_3_q3, ~shift_register_2_q3, ~shift_register_1_q3);  // AND_Gate
  D_Flip_Flop d_ff_1 (
    .clk(MOVE_FROM_B), .D(shift_register_1_q3), .Q(d_ff_1_q), .reset(MOVE_FROM_B_2));  // open: Qn, preset, en
  assign controlled_buffer_1_out = d_ff_1_q ? shift_register_1_out : 1'bz;  // Controlled_Buffer controlled_buffer_1
  D_Flip_Flop d_ff_2 (.clk(MOVE_FROM_B), .D(and_19_out), .Q(d_ff_2_q), .reset(MOVE_FROM_B_2));  // open: Qn, preset, en
  assign controlled_buffer_1_out = d_ff_2_q ? shift_register_2_out : 1'bz;  // Controlled_Buffer controlled_buffer_2
  D_Flip_Flop d_ff_3 (.clk(MOVE_FROM_B), .D(and_20_out), .Q(d_ff_3_q), .reset(MOVE_FROM_B_2));  // open: Qn, preset, en
  assign controlled_buffer_1_out = d_ff_3_q ? shift_register_3_out : 1'bz;  // Controlled_Buffer controlled_buffer_3
  D_Flip_Flop d_ff_4 (.clk(MOVE_FROM_B), .D(and_21_out), .Q(d_ff_4_q), .reset(MOVE_FROM_B_2));  // open: Qn, preset, en
  assign controlled_buffer_1_out = d_ff_4_q ? shift_register_4_out : 1'bz;  // Controlled_Buffer controlled_buffer_4
  Multiplexer #(.enable("false")) multiplexer_5 (
    .in0(1'b0), .in1(controlled_buffer_1_out), .out(multiplexer_5_out), .sel(MOVE_TO_B_2));
  Multiplexer #(.enable("false")) multiplexer_6 (
    .in0(1'b0), .in1(controlled_buffer_1_out), .out(multiplexer_6_out), .sel(MOVE_TO_B_2));
  Multiplexer #(.enable("false")) multiplexer_7 (
    .in0(1'b0), .in1(controlled_buffer_1_out), .out(multiplexer_7_out), .sel(MOVE_TO_B_2));
  Multiplexer #(.enable("false")) multiplexer_8 (
    .in0(1'b0), .in1(controlled_buffer_1_out), .out(multiplexer_8_out), .sel(MOVE_TO_B_2));
  and and_22 (and_22_out, MOVE_TO_B_2, ~and_23_out, ~and_24_out, ~and_25_out, ~shift_register_5_q3);  // AND_Gate
  and and_23 (and_23_out, MOVE_TO_B_2, ~and_25_out, ~and_24_out, ~shift_register_6_q3);  // AND_Gate
  and and_24 (and_24_out, MOVE_TO_B_2, ~and_25_out, ~shift_register_7_q3);  // AND_Gate
  and and_25 (and_25_out, MOVE_TO_B_2, ~shift_register_8_q3);  // AND_Gate
  and and_26 (and_26_out, d_ff_8_q, MOVE_FROM_B_2);
  and and_27 (and_27_out, d_ff_5_q, MOVE_FROM_B_2);
  and and_28 (and_28_out, d_ff_6_q, MOVE_FROM_B_2);
  ExactlyOne xor_5 (.out(xor_5_out), .in0(and_28_out), .in1(or_2_out), .in2(and_23_out));
  and and_29 (and_29_out, d_ff_7_q, MOVE_FROM_B_2);
  ExactlyOne xor_6 (.out(xor_6_out), .in0(and_29_out), .in1(or_2_out), .in2(and_24_out));
  ExactlyOne xor_7 (.out(xor_7_out), .in0(and_26_out), .in1(or_2_out), .in2(and_25_out));
  Shift_Register #(.length(4)) shift_register_5 (
    .in(multiplexer_5_out), .clk(and_30_out), .out(shift_register_5_out), .q0(shift_register_5_q0),
    .q1(shift_register_5_q1), .q2(shift_register_5_q2), .q3(shift_register_5_q3));  // open: shift, load, clr, d0, d1, d2, d3
  ExactlyOne xor_8 (.out(xor_8_out), .in0(and_27_out), .in1(or_2_out), .in2(and_22_out));
  and and_30 (and_30_out, xor_8_out, or_4_out);
  Shift_Register #(.length(4)) shift_register_6 (
    .in(multiplexer_6_out), .clk(and_31_out), .out(shift_register_6_out), .q0(shift_register_6_q0),
    .q1(shift_register_6_q1), .q2(shift_register_6_q2), .q3(shift_register_6_q3));  // open: shift, load, clr, d0, d1, d2, d3
  and and_31 (and_31_out, xor_5_out, or_4_out);
  Shift_Register #(.length(4)) shift_register_7 (
    .in(multiplexer_7_out), .clk(and_32_out), .out(shift_register_7_out), .q0(shift_register_7_q0),
    .q1(shift_register_7_q1), .q2(shift_register_7_q2), .q3(shift_register_7_q3));  // open: shift, load, clr, d0, d1, d2, d3
  and and_32 (and_32_out, xor_6_out, or_4_out);
  Shift_Register #(.length(4)) shift_register_8 (
    .in(multiplexer_8_out), .clk(and_33_out), .out(shift_register_8_out), .q0(shift_register_8_q0),
    .q1(shift_register_8_q1), .q2(shift_register_8_q2), .q3(shift_register_8_q3));  // open: shift, load, clr, d0, d1, d2, d3
  and and_33 (and_33_out, xor_7_out, or_4_out);
  DotMatrix #(.matrixcols(7), .matrixrows(1)) dotmatrix_5 (
    .col0(shift_register_5_q0), .col1(shift_register_5_q1), .col2(shift_register_5_q2),
    .col3(shift_register_5_q3), .col4(shift_register_5_q2), .col5(shift_register_5_q1),
    .col6(shift_register_5_q0));
  DotMatrix #(.matrixcols(7), .matrixrows(1)) dotmatrix_6 (
    .col0(shift_register_6_q0), .col1(shift_register_6_q1), .col2(shift_register_6_q2),
    .col3(shift_register_6_q3), .col4(shift_register_6_q2), .col5(shift_register_6_q1),
    .col6(shift_register_6_q0));
  DotMatrix #(.matrixcols(7), .matrixrows(1)) dotmatrix_7 (
    .col0(shift_register_7_q0), .col1(shift_register_7_q1), .col2(shift_register_7_q2),
    .col3(shift_register_7_q3), .col4(shift_register_7_q2), .col5(shift_register_7_q1),
    .col6(shift_register_7_q0));
  DotMatrix #(.matrixcols(7), .matrixrows(1)) dotmatrix_8 (
    .col0(shift_register_8_q0), .col1(shift_register_8_q1), .col2(shift_register_8_q2),
    .col3(shift_register_8_q3), .col4(shift_register_8_q2), .col5(shift_register_8_q1),
    .col6(shift_register_8_q0));
  and and_34 (and_34_out, shift_register_6_q3, ~shift_register_5_q3);  // AND_Gate
  and and_35 (and_35_out, shift_register_7_q3, ~shift_register_6_q3, ~shift_register_5_q3);  // AND_Gate
  and and_36 (and_36_out, shift_register_8_q3, ~shift_register_7_q3, ~shift_register_6_q3, ~shift_register_5_q3);  // AND_Gate
  D_Flip_Flop d_ff_5 (
    .clk(MOVE_FROM_B_2), .D(shift_register_5_q3), .Q(d_ff_5_q), .reset(MOVE_FROM_B));  // open: Qn, preset, en
  assign controlled_buffer_1_out = d_ff_5_q ? shift_register_5_out : 1'bz;  // Controlled_Buffer controlled_buffer_5
  D_Flip_Flop d_ff_6 (.clk(MOVE_FROM_B_2), .D(and_34_out), .Q(d_ff_6_q), .reset(MOVE_FROM_B));  // open: Qn, preset, en
  assign controlled_buffer_1_out = d_ff_6_q ? shift_register_6_out : 1'bz;  // Controlled_Buffer controlled_buffer_6
  D_Flip_Flop d_ff_7 (.clk(MOVE_FROM_B_2), .D(and_35_out), .Q(d_ff_7_q), .reset(MOVE_FROM_B));  // open: Qn, preset, en
  assign controlled_buffer_1_out = d_ff_7_q ? shift_register_7_out : 1'bz;  // Controlled_Buffer controlled_buffer_7
  D_Flip_Flop d_ff_8 (.clk(MOVE_FROM_B_2), .D(and_36_out), .Q(d_ff_8_q), .reset(MOVE_FROM_B));  // open: Qn, preset, en
  assign controlled_buffer_1_out = d_ff_8_q ? shift_register_8_out : 1'bz;  // Controlled_Buffer controlled_buffer_8

  // Notes on the sheet:
  //   push 4
  //   reset logic
  //   reset
  //   data bus
endmodule
