// Logisim project DSFFinal.circ as structural Verilog: 1 circuit, main circuit main
module main (
  input  move_from,
  input  move_from_2,
  input  move_to,
  input  move_to_2
);

  wire and_1_out, and_2_out, and_3_out, button_1_out, button_2_out, button_3_out, clock_1_out,
       controlled_buffer_1_out, counter_1_carry, counter_2_carry, multiplexer_1_out, multiplexer_2_out,
       multiplexer_3_out, multiplexer_4_out, multiplexer_5_out, multiplexer_6_out, multiplexer_7_out,
       multiplexer_8_out, multiplexer_9_out, multiplexer_10_out, multiplexer_11_out, multiplexer_12_out,
       nand_1_out, nand_2_out, nand_3_out, not_1_out, or_1_out, or_2_out, shift_register_1_out,
       shift_register_1_q0, shift_register_1_q1, shift_register_1_q2, shift_register_1_q3,
       shift_register_2_out, shift_register_2_q0, shift_register_2_q1, shift_register_2_q2,
       shift_register_2_q3, shift_register_3_out, shift_register_3_q0, shift_register_3_q1,
       shift_register_3_q2, shift_register_3_q3, shift_register_4_out, shift_register_4_q0,
       shift_register_4_q1, shift_register_4_q2, shift_register_4_q3, shift_register_5_out,
       shift_register_5_q0, shift_register_5_q1, shift_register_5_q2, shift_register_5_q3,
       shift_register_6_out, shift_register_6_q0, shift_register_6_q1, shift_register_6_q2,
       shift_register_6_q3, shift_register_7_out, shift_register_7_q0, shift_register_7_q1,
       shift_register_7_q2, shift_register_7_q3, shift_register_8_out, shift_register_8_q0,
       shift_register_8_q1, shift_register_8_q2, shift_register_8_q3, shift_register_9_out,
       shift_register_9_q0, shift_register_9_q1, shift_register_9_q2, shift_register_9_q3,
       shift_register_10_out, shift_register_10_q0, shift_register_10_q1, shift_register_10_q2,
       shift_register_10_q3, shift_register_11_out, shift_register_11_q0, shift_register_11_q1,
       shift_register_11_q2, shift_register_11_q3, shift_register_12_out, shift_register_12_q0,
       shift_register_12_q1, shift_register_12_q2, shift_register_12_q3, xor_1_out;
  wire [1:0] counter_1_q;

  or or_1 (or_1_out, button_2_out, ~counter_1_carry);  // OR_Gate
  Clock clock_1 (.out(clock_1_out));
  or or_2 (or_2_out, button_1_out, ~counter_2_carry);  // OR_Gate
  _7_Segment_Display u_7_segment_display_1 ();  // open: g, f, a, b, e, d, c, dp
  nand nand_1 (nand_1_out, or_1_out, clock_1_out);
  Button button_1 (.out(button_1_out));
  nand nand_2 (nand_2_out, or_2_out, clock_1_out);
  Button button_2 (.out(button_2_out));
  Counter #(.width(2), .max('h3)) counter_1 (
    .Q(counter_1_q), .carry(counter_1_carry), .clk(nand_1_out));  // open: load, D, count, clr
  Counter #(.width(2), .max('h3)) counter_2 (
    .carry(counter_2_carry), .clk(nand_2_out));  // open: load, D, count, Q, clr
  not not_1 (not_1_out, counter_1_q[0]);
  and and_1 (and_1_out, not_1_out, counter_1_q[1]);
  xor xor_1 (xor_1_out, counter_1_q[0], counter_1_q[1]);
  nand nand_3 (nand_3_out, counter_1_q[0], counter_1_q[1]);
  Multiplexer #(.enable("false")) multiplexer_1 (
    .in0(and_1_out), .out(multiplexer_1_out), .sel(nand_1_out));  // open: in1
  Multiplexer #(.enable("false")) multiplexer_2 (
    .in0(xor_1_out), .out(multiplexer_2_out), .sel(nand_1_out));  // open: in1
  Multiplexer #(.enable("false")) multiplexer_3 (
    .in0(nand_3_out), .out(multiplexer_3_out), .sel(nand_1_out));  // open: in1
  Multiplexer #(.enable("false")) multiplexer_4 (.in0(1'b1), .out(multiplexer_4_out), .sel(nand_1_out));  // open: in1
  Shift_Register #(.length(4)) shift_register_1 (
    .in(multiplexer_1_out), .clk(and_2_out), .out(shift_register_1_out), .q0(shift_register_1_q0),
    .q1(shift_register_1_q1), .q2(shift_register_1_q2), .q3(shift_register_1_q3));  // open: shift, load, clr, d0, d1, d2, d3
  and and_2 (and_2_out, nand_2_out, nand_1_out);
  Shift_Register #(.length(4)) shift_register_2 (
    .in(multiplexer_2_out), .clk(nand_1_out), .out(shift_register_2_out), .q0(shift_register_2_q0),
    .q1(shift_register_2_q1), .q2(shift_register_2_q2), .q3(shift_register_2_q3));  // open: shift, load, clr, d0, d1, d2, d3
  Shift_Register #(.length(4)) shift_register_3 (
    .in(multiplexer_3_out), .clk(nand_1_out), .out(shift_register_3_out), .q0(shift_register_3_q0),
    .q1(shift_register_3_q1), .q2(shift_register_3_q2), .q3(shift_register_3_q3));  // open: shift, load, clr, d0, d1, d2, d3
  Shift_Register #(.length(4)) shift_register_4 (
    .in(multiplexer_4_out), .clk(nand_1_out), .out(shift_register_4_out), .q0(shift_register_4_q0),
    .q1(shift_register_4_q1), .q2(shift_register_4_q2), .q3(shift_register_4_q3));  // open: shift, load, clr, d0, d1, d2, d3
  DotMatrix #(.matrixcols(7), .matrixrows(1)) dotmatrix_1 (
    .col0(shift_register_1_q3), .col1(shift_register_1_q2), .col2(shift_register_1_q1),
    .col3(shift_register_1_q0), .col4(shift_register_1_q1), .col5(shift_register_1_q2),
    .col6(shift_register_1_q3));
  DotMatrix #(.matrixcols(7), .matrixrows(1)) dotmatrix_2 (
    .col0(shift_register_2_q3), .col1(shift_register_2_q2), .col2(shift_register_2_q1),
    .col3(shift_register_2_q0), .col4(shift_register_2_q1), .col5(shift_register_2_q2),
    .col6(shift_register_2_q3));
  DotMatrix #(.matrixcols(7), .matrixrows(1)) dotmatrix_3 (
    .col0(shift_register_3_q3), .col1(shift_register_3_q2), .col2(shift_register_3_q1),
    .col3(shift_register_3_q0), .col4(shift_register_3_q1), .col5(shift_register_3_q2),
    .col6(shift_register_3_q3));
  DotMatrix #(.matrixcols(7), .matrixrows(1)) dotmatrix_4 (
    .col0(shift_register_4_q3), .col1(shift_register_4_q2), .col2(shift_register_4_q1),
    .col3(shift_register_4_q0), .col4(shift_register_4_q1), .col5(shift_register_4_q2),
    .col6(shift_register_4_q3));
  assign controlled_buffer_1_out = move_from ? shift_register_1_out : 1'bz;  // Controlled_Buffer controlled_buffer_1
  Controlled_Buffer controlled_buffer_2 (.in(shift_register_2_out));  // open: out, en
  Controlled_Buffer controlled_buffer_3 (.in(shift_register_3_out));  // open: out, en
  Controlled_Buffer controlled_buffer_4 (.in(shift_register_4_out));  // open: out, en
  Multiplexer #(.enable("false")) multiplexer_5 (.in0(1'b0), .out(multiplexer_5_out), .sel(nand_1_out));  // open: in1
  Multiplexer #(.enable("false")) multiplexer_6 (.in0(1'b0), .out(multiplexer_6_out), .sel(nand_1_out));  // open: in1
  Multiplexer #(.enable("false")) multiplexer_7 (.in0(1'b0), .out(multiplexer_7_out), .sel(nand_1_out));  // open: in1
  Multiplexer #(.enable("false")) multiplexer_8 (
    .in0(1'b0), .in1(controlled_buffer_1_out), .out(multiplexer_8_out), .sel(nand_1_out));
  Shift_Register #(.length(4)) shift_register_5 (
    .in(multiplexer_5_out), .out(shift_register_5_out), .q0(shift_register_5_q0), .q1(shift_register_5_q1),
    .q2(shift_register_5_q2), .q3(shift_register_5_q3));  // open: shift, clk, load, clr, d0, d1, d2, d3
  Shift_Register #(.length(4)) shift_register_6 (
    .in(multiplexer_6_out), .clk(nand_1_out), .out(shift_register_6_out), .q0(shift_register_6_q0),
    .q1(shift_register_6_q1), .q2(shift_register_6_q2), .q3(shift_register_6_q3));  // open: shift, load, clr, d0, d1, d2, d3
  Shift_Register #(.length(4)) shift_register_7 (
    .in(multiplexer_7_out), .clk(nand_1_out), .out(shift_register_7_out), .q0(shift_register_7_q0),
    .q1(shift_register_7_q1), .q2(shift_register_7_q2), .q3(shift_register_7_q3));  // open: shift, load, clr, d0, d1, d2, d3
  Shift_Register #(.length(4)) shift_register_8 (
    .in(multiplexer_8_out), .clk(and_3_out), .out(shift_register_8_out), .q0(shift_register_8_q0),
    .q1(shift_register_8_q1), .q2(shift_register_8_q2), .q3(shift_register_8_q3));  // open: shift, load, clr, d0, d1, d2, d3
  and and_3 (and_3_out, nand_2_out, nand_1_out);
  DotMatrix #(.matrixcols(7), .matrixrows(1)) dotmatrix_5 (
    .col0(shift_register_5_q3), .col1(shift_register_5_q2), .col2(shift_register_5_q1),
    .col3(shift_register_5_q0), .col4(shift_register_5_q1), .col5(shift_register_5_q2),
    .col6(shift_register_5_q3));
  DotMatrix #(.matrixcols(7), .matrixrows(1)) dotmatrix_6 (
    .col0(shift_register_6_q3), .col1(shift_register_6_q2), .col2(shift_register_6_q1),
    .col3(shift_register_6_q0), .col4(shift_register_6_q1), .col5(shift_register_6_q2),
    .col6(shift_register_6_q3));
  DotMatrix #(.matrixcols(7), .matrixrows(1)) dotmatrix_7 (
    .col0(shift_register_7_q3), .col1(shift_register_7_q2), .col2(shift_register_7_q1),
    .col3(shift_register_7_q0), .col4(shift_register_7_q1), .col5(shift_register_7_q2),
    .col6(shift_register_7_q3));
  DotMatrix #(.matrixcols(7), .matrixrows(1)) dotmatrix_8 (
    .col0(shift_register_8_q3), .col1(shift_register_8_q2), .col2(shift_register_8_q1),
    .col3(shift_register_8_q0), .col4(shift_register_8_q1), .col5(shift_register_8_q2),
    .col6(shift_register_8_q3));
  Controlled_Buffer controlled_buffer_5 (.in(shift_register_5_out));  // open: out, en
  Controlled_Buffer controlled_buffer_6 (.in(shift_register_6_out));  // open: out, en
  Controlled_Buffer controlled_buffer_7 (.in(shift_register_7_out));  // open: out, en
  Controlled_Buffer controlled_buffer_8 (.in(shift_register_8_out));  // open: out, en
  Multiplexer #(.enable("false")) multiplexer_9 (.in0(1'b0), .out(multiplexer_9_out), .sel(nand_1_out));  // open: in1
  Multiplexer #(.enable("false")) multiplexer_10 (.in0(1'b0), .out(multiplexer_10_out), .sel(nand_1_out));  // open: in1
  Multiplexer #(.enable("false")) multiplexer_11 (.in0(1'b0), .out(multiplexer_11_out), .sel(nand_1_out));  // open: in1
  Multiplexer #(.enable("false")) multiplexer_12 (.in0(1'b0), .out(multiplexer_12_out), .sel(nand_1_out));  // open: in1
  Shift_Register #(.length(4)) shift_register_9 (
    .in(multiplexer_9_out), .clk(nand_1_out), .out(shift_register_9_out), .q0(shift_register_9_q0),
    .q1(shift_register_9_q1), .q2(shift_register_9_q2), .q3(shift_register_9_q3));  // open: shift, load, clr, d0, d1, d2, d3
  Shift_Register #(.length(4)) shift_register_10 (
    .in(multiplexer_10_out), .clk(nand_1_out), .out(shift_register_10_out), .q0(shift_register_10_q0),
    .q1(shift_register_10_q1), .q2(shift_register_10_q2), .q3(shift_register_10_q3));  // open: shift, load, clr, d0, d1, d2, d3
  Shift_Register #(.length(4)) shift_register_11 (
    .in(multiplexer_11_out), .clk(nand_1_out), .out(shift_register_11_out), .q0(shift_register_11_q0),
    .q1(shift_register_11_q1), .q2(shift_register_11_q2), .q3(shift_register_11_q3));  // open: shift, load, clr, d0, d1, d2, d3
  Shift_Register #(.length(4)) shift_register_12 (
    .in(multiplexer_12_out), .clk(nand_1_out), .out(shift_register_12_out), .q0(shift_register_12_q0),
    .q1(shift_register_12_q1), .q2(shift_register_12_q2), .q3(shift_register_12_q3));  // open: shift, load, clr, d0, d1, d2, d3
  Button button_3 (.out(button_3_out));
  Button button_4 ();  // open: out
  DotMatrix #(.matrixcols(7), .matrixrows(1)) dotmatrix_9 (
    .col0(shift_register_9_q3), .col1(shift_register_9_q2), .col2(shift_register_9_q1),
    .col3(shift_register_9_q0), .col4(shift_register_9_q1), .col5(shift_register_9_q2),
    .col6(shift_register_9_q3));
  DotMatrix #(.matrixcols(7), .matrixrows(1)) dotmatrix_10 (
    .col0(shift_register_10_q3), .col1(shift_register_10_q2), .col2(shift_register_10_q1),
    .col3(shift_register_10_q0), .col4(shift_register_10_q1), .col5(shift_register_10_q2),
    .col6(shift_register_10_q3));
  DotMatrix #(.matrixcols(7), .matrixrows(1)) dotmatrix_11 (
    .col0(shift_register_11_q3), .col1(shift_register_11_q2), .col2(shift_register_11_q1),
    .col3(shift_register_11_q0), .col4(shift_register_11_q1), .col5(shift_register_11_q2),
    .col6(shift_register_11_q3));
  DotMatrix #(.matrixcols(7), .matrixrows(1)) dotmatrix_12 (
    .col0(shift_register_12_q3), .col1(shift_register_12_q2), .col2(shift_register_12_q1),
    .col3(shift_register_12_q0), .col4(shift_register_12_q1), .col5(shift_register_12_q2),
    .col6(shift_register_12_q3));
  D_Flip_Flop d_ff_1 (.clk(button_3_out), .D(button_3_out));  // open: Q, Qn, preset, en, reset
  Controlled_Buffer controlled_buffer_9 (.in(shift_register_9_out));  // open: out, en
  Controlled_Buffer controlled_buffer_10 (.in(shift_register_10_out));  // open: out, en
  Controlled_Buffer controlled_buffer_11 (.in(shift_register_11_out));  // open: out, en
  Controlled_Buffer controlled_buffer_12 (.in(shift_register_12_out));  // open: out, en

  // Notes on the sheet:
  //   reset logic
  //   reset
  //   push 4
  //   data bus
  //   column a
  //   column b
  //   column c
  //   move from
  //   move to
endmodule
