// Logisim project DSFFinal.circ as structural Verilog: 1 circuit, main circuit main
module main (
  input  MOVE_FROM_A,
  input  MOVE_FROM_B,
  input  MOVE_FROM_C,
  input  MOVE_TO_A,
  input  MOVE_TO_B,
  input  MOVE_TO_C
);

  wire and_1_out, and_2_out, and_3_out, and_4_out, and_5_out, and_6_out, and_7_out, and_8_out, and_9_out,
       and_10_out, and_11_out, and_12_out, and_13_out, and_14_out, and_15_out, and_16_out, and_17_out,
       and_18_out, and_20_out, and_21_out, and_22_out, and_23_out, and_24_out, and_25_out, and_26_out,
       and_27_out, and_28_out, and_29_out, and_30_out, and_31_out, and_32_out, and_33_out, and_34_out,
       and_35_out, and_36_out, button_1_out, button_2_out, clock_1_out, controlled_buffer_1_out,
       counter_1_carry, counter_2_carry, multiplexer_1_out, multiplexer_2_out, multiplexer_3_out,
       multiplexer_4_out, multiplexer_5_out, multiplexer_6_out, multiplexer_7_out, multiplexer_8_out,
       multiplexer_9_out, multiplexer_10_out, multiplexer_11_out, multiplexer_12_out, nand_1_out, or_1_out,
       or_2_out, or_3_out, or_4_out, or_5_out, or_6_out, or_7_out, or_8_out, or_9_out, or_10_out, or_11_out,
       or_12_out, or_13_out, or_14_out, shift_register_1_out, shift_register_1_q0, shift_register_1_q1,
       shift_register_1_q2, shift_register_1_q3, shift_register_2_out, shift_register_2_q0,
       shift_register_2_q1, shift_register_2_q2, shift_register_2_q3, shift_register_3_out,
       shift_register_3_q0, shift_register_3_q1, shift_register_3_q2, shift_register_3_q3,
       shift_register_4_out, shift_register_4_q0, shift_register_4_q1, shift_register_4_q2,
       shift_register_4_q3, shift_register_5_out, shift_register_5_q0, shift_register_5_q1,
       shift_register_5_q2, shift_register_5_q3, shift_register_6_out, shift_register_6_q0,
       shift_register_6_q1, shift_register_6_q2, shift_register_6_q3, shift_register_7_out,
       shift_register_7_q0, shift_register_7_q1, shift_register_7_q2, shift_register_7_q3,
       shift_register_8_out, shift_register_8_q0, shift_register_8_q1, shift_register_8_q2,
       shift_register_8_q3, shift_register_9_out, shift_register_9_q0, shift_register_9_q1,
       shift_register_9_q2, shift_register_9_q3, shift_register_10_out, shift_register_10_q0,
       shift_register_10_q1, shift_register_10_q2, shift_register_10_q3, shift_register_11_out,
       shift_register_11_q0, shift_register_11_q1, shift_register_11_q2, shift_register_11_q3,
       shift_register_12_out, shift_register_12_q0, shift_register_12_q1, shift_register_12_q2,
       shift_register_12_q3, undriven, xor_1_out;
  wire [1:0] counter_1_q;

  or or_1 (or_1_out, button_2_out, ~counter_1_carry);  // OR_Gate
  Clock clock_1 (.out(clock_1_out));
  or or_2 (or_2_out, button_1_out, ~counter_2_carry);  // OR_Gate
  and and_1 (and_1_out, or_1_out, clock_1_out);
  Button button_1 (.out(button_1_out));
  and and_2 (and_2_out, or_2_out, clock_1_out);
  Button button_2 (.out(button_2_out));
  Counter #(.width(2), .max('h3)) counter_1 (
    .Q(counter_1_q), .carry(counter_1_carry), .clk(and_1_out));  // open: load, D, count, clr
  Counter #(.width(2), .max('h3)) counter_2 (.carry(counter_2_carry), .clk(and_2_out));  // open: load, D, count, Q, clr
  and and_3 (and_3_out, ~counter_1_q[0], counter_1_q[1]);  // AND_Gate
  xor xor_1 (xor_1_out, counter_1_q[0], counter_1_q[1]);
  nand nand_1 (nand_1_out, counter_1_q[0], counter_1_q[1]);
  Multiplexer #(.enable("false")) multiplexer_1 (
    .in0(and_3_out), .in1(controlled_buffer_1_out), .out(multiplexer_1_out), .sel(and_1_out));
  Multiplexer #(.enable("false")) multiplexer_2 (
    .in0(xor_1_out), .in1(controlled_buffer_1_out), .out(multiplexer_2_out), .sel(and_1_out));
  Multiplexer #(.enable("false")) multiplexer_3 (
    .in0(nand_1_out), .in1(controlled_buffer_1_out), .out(multiplexer_3_out), .sel(and_1_out));
  Multiplexer #(.enable("false")) multiplexer_4 (
    .in0(1'b1), .in1(controlled_buffer_1_out), .out(multiplexer_4_out), .sel(and_1_out));
  and and_4 (and_4_out, shift_register_1_q0, MOVE_TO_A, and_2_out);
  and and_5 (and_5_out, and_8_out, MOVE_TO_A, and_2_out);
  and and_6 (and_6_out, and_9_out, MOVE_TO_A, and_2_out);
  and and_7 (and_7_out, and_10_out, MOVE_TO_A, and_2_out);
  Shift_Register #(.length(4)) shift_register_1 (
    .in(multiplexer_1_out), .clk(or_3_out), .out(shift_register_1_out), .q0(shift_register_1_q0),
    .q1(shift_register_1_q1), .q2(shift_register_1_q2), .q3(shift_register_1_q3));  // open: shift, load, clr, d0, d1, d2, d3
  or or_3 (or_3_out, and_4_out, and_1_out);
  Shift_Register #(.length(4)) shift_register_2 (
    .in(multiplexer_2_out), .clk(or_4_out), .out(shift_register_2_out), .q0(shift_register_2_q0),
    .q1(shift_register_2_q1), .q2(shift_register_2_q2), .q3(shift_register_2_q3));  // open: shift, load, clr, d0, d1, d2, d3
  or or_4 (or_4_out, and_5_out, and_1_out);
  Shift_Register #(.length(4)) shift_register_3 (
    .in(multiplexer_3_out), .clk(or_5_out), .out(shift_register_3_out), .q0(shift_register_3_q0),
    .q1(shift_register_3_q1), .q2(shift_register_3_q2), .q3(shift_register_3_q3));  // open: shift, load, clr, d0, d1, d2, d3
  or or_5 (or_5_out, and_6_out, and_1_out);
  Shift_Register #(.length(4)) shift_register_4 (
    .in(multiplexer_4_out), .clk(or_6_out), .out(shift_register_4_out), .q0(shift_register_4_q0),
    .q1(shift_register_4_q1), .q2(shift_register_4_q2), .q3(shift_register_4_q3));  // open: shift, load, clr, d0, d1, d2, d3
  or or_6 (or_6_out, and_7_out, and_1_out);
  DotMatrix #(.matrixcols(7), .matrixrows(1)) dotmatrix_1 (
    .col0(shift_register_1_q3), .col1(shift_register_1_q2), .col2(shift_register_1_q1),
    .col3(shift_register_1_q0), .col4(shift_register_1_q1), .col5(shift_register_1_q2),
    .col6(shift_register_1_q3));
  DotMatrix #(.matrixcols(7), .matrixrows(1)) dotmatrix_2 (
    .col0(shift_register_2_q3), .col1(shift_register_2_q2), .col2(shift_register_2_q1),
    .col3(shift_register_2_q0), .col4(shift_register_2_q1), .col5(shift_register_2_q2),
    .col6(shift_register_2_q3));
  DotMatrix #(.matrixcols(7), .matrixrows(1)) dotmatrix_3 (
    .col0(shift_register_3_q3), .col1(shift_register_3_q2), .col2(shift_register_3_q1),
    .col3(shift_register_3_q0), .col4(shift_register_3_q1), .col5(shift_register_3_q2),
    .col6(shift_register_3_q3));
  DotMatrix #(.matrixcols(7), .matrixrows(1)) dotmatrix_4 (
    .col0(shift_register_4_q3), .col1(shift_register_4_q2), .col2(shift_register_4_q1),
    .col3(shift_register_4_q0), .col4(shift_register_4_q1), .col5(shift_register_4_q2),
    .col6(shift_register_4_q3));
  and and_8 (and_8_out, shift_register_2_q0, ~shift_register_1_q0);  // AND_Gate
  and and_9 (and_9_out, shift_register_3_q0, ~shift_register_2_q0, ~shift_register_1_q0);  // AND_Gate
  and and_10 (and_10_out, shift_register_4_q0, ~shift_register_3_q0, ~shift_register_2_q0, ~shift_register_1_q0);  // AND_Gate
  and and_11 (and_11_out, shift_register_1_q0, MOVE_FROM_A);
  assign controlled_buffer_1_out = and_11_out ? shift_register_1_out : 1'bz;  // Controlled_Buffer controlled_buffer_1
  and and_12 (and_12_out, and_8_out, MOVE_FROM_A);
  assign controlled_buffer_1_out = and_12_out ? shift_register_2_out : 1'bz;  // Controlled_Buffer controlled_buffer_2
  and and_13 (and_13_out, and_9_out, MOVE_FROM_A);
  assign controlled_buffer_1_out = and_13_out ? shift_register_3_out : 1'bz;  // Controlled_Buffer controlled_buffer_3
  and and_14 (and_14_out, and_10_out, MOVE_FROM_A);
  assign controlled_buffer_1_out = and_14_out ? shift_register_4_out : 1'bz;  // Controlled_Buffer controlled_buffer_4
  Multiplexer #(.enable("false")) multiplexer_5 (
    .in0(1'b0), .in1(controlled_buffer_1_out), .out(multiplexer_5_out), .sel(and_1_out));
  Multiplexer #(.enable("false")) multiplexer_6 (
    .in0(1'b0), .in1(controlled_buffer_1_out), .out(multiplexer_6_out), .sel(and_1_out));
  Multiplexer #(.enable("false")) multiplexer_7 (
    .in0(1'b0), .in1(controlled_buffer_1_out), .out(multiplexer_7_out), .sel(and_1_out));
  Multiplexer #(.enable("false")) multiplexer_8 (
    .in0(1'b0), .in1(controlled_buffer_1_out), .out(multiplexer_8_out), .sel(and_1_out));
  and and_15 (and_15_out, shift_register_5_q0, MOVE_TO_B, and_2_out);
  or or_7 (or_7_out, and_15_out, and_1_out);
  and and_16 (and_16_out, undriven, MOVE_TO_B, and_2_out);
  or or_8 (or_8_out, and_16_out, and_1_out);
  and and_17 (and_17_out, and_20_out, MOVE_TO_B, and_2_out);
  or or_9 (or_9_out, and_17_out, and_1_out);
  and and_18 (and_18_out, and_21_out, MOVE_TO_B, and_2_out);
  or or_10 (or_10_out, and_18_out, and_1_out);
  Shift_Register #(.length(4)) shift_register_5 (
    .in(multiplexer_5_out), .clk(or_7_out), .out(shift_register_5_out), .q0(shift_register_5_q0),
    .q1(shift_register_5_q1), .q2(shift_register_5_q2), .q3(shift_register_5_q3));  // open: shift, load, clr, d0, d1, d2, d3
  Shift_Register #(.length(4)) shift_register_6 (
    .in(multiplexer_6_out), .clk(or_8_out), .out(shift_register_6_out), .q0(shift_register_6_q0),
    .q1(shift_register_6_q1), .q2(shift_register_6_q2), .q3(shift_register_6_q3));  // open: shift, load, clr, d0, d1, d2, d3
  Shift_Register #(.length(4)) shift_register_7 (
    .in(multiplexer_7_out), .clk(or_9_out), .out(shift_register_7_out), .q0(shift_register_7_q0),
    .q1(shift_register_7_q1), .q2(shift_register_7_q2), .q3(shift_register_7_q3));  // open: shift, load, clr, d0, d1, d2, d3
  Shift_Register #(.length(4)) shift_register_8 (
    .in(multiplexer_8_out), .clk(or_10_out), .out(shift_register_8_out), .q0(shift_register_8_q0),
    .q1(shift_register_8_q1), .q2(shift_register_8_q2), .q3(shift_register_8_q3));  // open: shift, load, clr, d0, d1, d2, d3
  DotMatrix #(.matrixcols(7), .matrixrows(1)) dotmatrix_5 (
    .col0(shift_register_5_q3), .col1(shift_register_5_q2), .col2(shift_register_5_q1),
    .col3(shift_register_5_q0), .col4(shift_register_5_q1), .col5(shift_register_5_q2),
    .col6(shift_register_5_q3));
  DotMatrix #(.matrixcols(7), .matrixrows(1)) dotmatrix_6 (
    .col0(shift_register_6_q3), .col1(shift_register_6_q2), .col2(shift_register_6_q1),
    .col3(shift_register_6_q0), .col4(shift_register_6_q1), .col5(shift_register_6_q2),
    .col6(shift_register_6_q3));
  DotMatrix #(.matrixcols(7), .matrixrows(1)) dotmatrix_7 (
    .col0(shift_register_7_q3), .col1(shift_register_7_q2), .col2(shift_register_7_q1),
    .col3(shift_register_7_q0), .col4(shift_register_7_q1), .col5(shift_register_7_q2),
    .col6(shift_register_7_q3));
  DotMatrix #(.matrixcols(7), .matrixrows(1)) dotmatrix_8 (
    .col0(shift_register_8_q3), .col1(shift_register_8_q2), .col2(shift_register_8_q1),
    .col3(shift_register_8_q0), .col4(shift_register_8_q1), .col5(shift_register_8_q2),
    .col6(shift_register_8_q3));
  // AND_Gate and_19 has open pins: in0=shift_register_6_q0, in1=shift_register_5_q0, out=open
  and and_20 (and_20_out, shift_register_7_q0, ~shift_register_6_q0, ~shift_register_5_q0);  // AND_Gate
  and and_21 (and_21_out, ~shift_register_7_q0, ~shift_register_6_q0, ~shift_register_5_q0);  // AND_Gate
  and and_22 (and_22_out, shift_register_5_q0, MOVE_FROM_B);
  assign controlled_buffer_1_out = and_22_out ? shift_register_5_out : 1'bz;  // Controlled_Buffer controlled_buffer_5
  and and_23 (and_23_out, undriven, MOVE_FROM_B);
  assign controlled_buffer_1_out = and_23_out ? shift_register_6_out : 1'bz;  // Controlled_Buffer controlled_buffer_6
  and and_24 (and_24_out, and_20_out, MOVE_FROM_B);
  assign controlled_buffer_1_out = and_24_out ? shift_register_7_out : 1'bz;  // Controlled_Buffer controlled_buffer_7
  and and_25 (and_25_out, and_21_out, MOVE_FROM_B);
  assign controlled_buffer_1_out = and_25_out ? shift_register_8_out : 1'bz;  // Controlled_Buffer controlled_buffer_8
  Multiplexer #(.enable("false")) multiplexer_9 (
    .in0(1'b0), .in1(controlled_buffer_1_out), .out(multiplexer_9_out), .sel(and_1_out));
  Multiplexer #(.enable("false")) multiplexer_10 (
    .in0(1'b0), .in1(controlled_buffer_1_out), .out(multiplexer_10_out), .sel(and_1_out));
  Multiplexer #(.enable("false")) multiplexer_11 (
    .in0(1'b0), .in1(controlled_buffer_1_out), .out(multiplexer_11_out), .sel(and_1_out));
  Multiplexer #(.enable("false")) multiplexer_12 (
    .in0(1'b0), .in1(controlled_buffer_1_out), .out(multiplexer_12_out), .sel(and_1_out));
  and and_26 (and_26_out, shift_register_9_q0, MOVE_TO_C, and_2_out);
  and and_27 (and_27_out, and_30_out, MOVE_TO_C, and_2_out);
  and and_28 (and_28_out, and_31_out, MOVE_TO_C, and_2_out);
  and and_29 (and_29_out, and_32_out, MOVE_TO_C, and_2_out);
  Shift_Register #(.length(4)) shift_register_9 (
    .in(multiplexer_9_out), .clk(or_11_out), .out(shift_register_9_out), .q0(shift_register_9_q0),
    .q1(shift_register_9_q1), .q2(shift_register_9_q2), .q3(shift_register_9_q3));  // open: shift, load, clr, d0, d1, d2, d3
  or or_11 (or_11_out, and_26_out, and_1_out);
  Shift_Register #(.length(4)) shift_register_10 (
    .in(multiplexer_10_out), .clk(or_12_out), .out(shift_register_10_out), .q0(shift_register_10_q0),
    .q1(shift_register_10_q1), .q2(shift_register_10_q2), .q3(shift_register_10_q3));  // open: shift, load, clr, d0, d1, d2, d3
  or or_12 (or_12_out, and_27_out, and_1_out);
  Shift_Register #(.length(4)) shift_register_11 (
    .in(multiplexer_11_out), .clk(or_13_out), .out(shift_register_11_out), .q0(shift_register_11_q0),
    .q1(shift_register_11_q1), .q2(shift_register_11_q2), .q3(shift_register_11_q3));  // open: shift, load, clr, d0, d1, d2, d3
  or or_13 (or_13_out, and_28_out, and_1_out);
  Shift_Register #(.length(4)) shift_register_12 (
    .in(multiplexer_12_out), .clk(or_14_out), .out(shift_register_12_out), .q0(shift_register_12_q0),
    .q1(shift_register_12_q1), .q2(shift_register_12_q2), .q3(shift_register_12_q3));  // open: shift, load, clr, d0, d1, d2, d3
  or or_14 (or_14_out, and_29_out, and_1_out);
  DotMatrix #(.matrixcols(7), .matrixrows(1)) dotmatrix_9 (
    .col0(shift_register_9_q3), .col1(shift_register_9_q2), .col2(shift_register_9_q1),
    .col3(shift_register_9_q0), .col4(shift_register_9_q1), .col5(shift_register_9_q2),
    .col6(shift_register_9_q3));
  DotMatrix #(.matrixcols(7), .matrixrows(1)) dotmatrix_10 (
    .col0(shift_register_10_q3), .col1(shift_register_10_q2), .col2(shift_register_10_q1),
    .col3(shift_register_10_q0), .col4(shift_register_10_q1), .col5(shift_register_10_q2),
    .col6(shift_register_10_q3));
  DotMatrix #(.matrixcols(7), .matrixrows(1)) dotmatrix_11 (
    .col0(shift_register_11_q3), .col1(shift_register_11_q2), .col2(shift_register_11_q1),
    .col3(shift_register_11_q0), .col4(shift_register_11_q1), .col5(shift_register_11_q2),
    .col6(shift_register_11_q3));
  DotMatrix #(.matrixcols(7), .matrixrows(1)) dotmatrix_12 (
    .col0(shift_register_12_q3), .col1(shift_register_12_q2), .col2(shift_register_12_q1),
    .col3(shift_register_12_q0), .col4(shift_register_12_q1), .col5(shift_register_12_q2),
    .col6(shift_register_12_q3));
  and and_30 (and_30_out, shift_register_10_q0, ~shift_register_9_q0);  // AND_Gate
  and and_31 (and_31_out, shift_register_11_q0, ~shift_register_10_q0, ~shift_register_9_q0);  // AND_Gate
  and and_32 (and_32_out, shift_register_12_q0, ~shift_register_11_q0, ~shift_register_10_q0, ~shift_register_9_q0);  // AND_Gate
  and and_33 (and_33_out, shift_register_9_q0, MOVE_FROM_C);
  assign controlled_buffer_1_out = and_33_out ? shift_register_9_out : 1'bz;  // Controlled_Buffer controlled_buffer_9
  and and_34 (and_34_out, and_30_out, MOVE_FROM_C);
  assign controlled_buffer_1_out = and_34_out ? shift_register_10_out : 1'bz;  // Controlled_Buffer controlled_buffer_10
  and and_35 (and_35_out, and_31_out, MOVE_FROM_C);
  assign controlled_buffer_1_out = and_35_out ? shift_register_11_out : 1'bz;  // Controlled_Buffer controlled_buffer_11
  and and_36 (and_36_out, and_32_out, MOVE_FROM_C);
  assign controlled_buffer_1_out = and_36_out ? shift_register_12_out : 1'bz;  // Controlled_Buffer controlled_buffer_12

  // Notes on the sheet:
  //   reset logic
  //   reset
  //   push 4
  //   data bus
endmodule
